// Logisim project ep1.circ as structural Verilog: 6 circuits, main circuit SomaSub
module Main (
  input  OP,
  input  [7:0] A,
  input  [7:0] B,
  output SS,
  output CS,
  output [7:0] R
);

  Circuito circuito_1 (.overflow_comSinal(CS), .R(R), .overflow_semSinal(SS), .A(A), .B(B), .OP(OP));  // open: out_6
endmodule

module Circuito (
  input  OP,
  input  [7:0] A,
  input  [7:0] B,
  output overflow_semSinal,
  output overflow_comSinal,
  output out_6,
  output [7:0] R
);

  wire not_1_out, somasub_1_c7;

  SomaSub somasub_1 (
    .R7(R[7]), .R6(R[6]), .R5(R[5]), .R4(R[4]), .R3(R[3]), .R2(R[2]), .R1(R[1]), .R0(R[0]), .Cout(out_6),
    .C7(somasub_1_c7), .OPsub(OP), .b7(B[7]), .b6(B[6]), .b5(A[5]), .b4(B[4]), .b3(B[3]), .b2(B[2]),
    .b1(B[1]), .b0(B[0]), .a7(A[7]), .a6(A[6]), .a5(B[5]), .a4(A[4]), .a3(A[3]), .a2(A[2]), .a1(A[1]),
    .a0(A[0]));
  not not_1 (not_1_out, out_6);
  Multiplexer #(.enable("false")) multiplexer_1 (.in0(out_6), .in1(not_1_out), .out(overflow_semSinal), .sel(OP));
  xor xor_1 (overflow_comSinal, out_6, somasub_1_c7);
endmodule

module SomaSub (
  input  OPsub,
  input  b7,
  input  b6,
  input  b5,
  input  a7,
  input  a6,
  input  a5,
  input  b4,
  input  a4,
  input  a3,
  input  b3,
  input  a2,
  input  a1,
  input  a0,
  input  b2,
  input  b1,
  input  b0,
  output R7,
  output R6,
  output R5,
  output R4,
  output R3,
  output R2,
  output R1,
  output R0,
  output C7,
  output Cout
);

  wire not_1_out, not_2_out, not_3_out, not_4_out, not_5_out, not_6_out, not_7_out, not_8_out,
       selector1bit_1_o, selector1bit_2_o, selector1bit_3_o, selector1bit_4_o, selector1bit_5_o,
       selector1bit_6_o, selector1bit_7_o, selector1bit_8_o;

  not not_1 (not_1_out, b7);
  not not_2 (not_2_out, b6);
  not not_3 (not_3_out, b5);
  not not_4 (not_4_out, b4);
  not not_5 (not_5_out, b3);
  not not_6 (not_6_out, b2);
  not not_7 (not_7_out, b1);
  not not_8 (not_8_out, b0);
  Selector1bit selector1bit_1 (.S(OPsub), .a0(b7), .a1(not_1_out), .o(selector1bit_1_o));
  Selector1bit selector1bit_2 (.S(OPsub), .a0(b6), .a1(not_2_out), .o(selector1bit_2_o));
  Selector1bit selector1bit_3 (.S(OPsub), .a0(b5), .a1(not_3_out), .o(selector1bit_3_o));
  Selector1bit selector1bit_4 (.S(OPsub), .a0(b4), .a1(not_4_out), .o(selector1bit_4_o));
  Selector1bit selector1bit_5 (.S(OPsub), .a0(b3), .a1(not_5_out), .o(selector1bit_5_o));
  Selector1bit selector1bit_6 (.S(OPsub), .a0(b2), .a1(not_6_out), .o(selector1bit_6_o));
  Selector1bit selector1bit_7 (.S(OPsub), .a0(b1), .a1(not_7_out), .o(selector1bit_7_o));
  Selector1bit selector1bit_8 (.S(OPsub), .a0(b0), .a1(not_8_out), .o(selector1bit_8_o));
  Somador8bits somador8bits_1 (
    .Cin(OPsub), .b7(selector1bit_1_o), .a7(a7), .b6(selector1bit_2_o), .a6(a6), .b5(selector1bit_3_o),
    .a5(a5), .b4(selector1bit_4_o), .a4(a4), .b3(selector1bit_5_o), .a3(a3), .b2(selector1bit_6_o), .a2(a2),
    .b1(selector1bit_7_o), .a1(a1), .b0(selector1bit_8_o), .a0(a0), .R7(R7), .R6(R6), .R5(R5), .R4(R4),
    .R3(R3), .R2(R2), .R1(R1), .C0(R0), .Cout(Cout), .C7(C7));
endmodule

module Somador8bits (
  input  Cin,
  input  b7,
  input  a7,
  input  b6,
  input  a6,
  input  b5,
  input  a5,
  input  b4,
  input  a4,
  input  b3,
  input  a3,
  input  b2,
  input  a2,
  input  b1,
  input  a1,
  input  b0,
  input  a0,
  output R7,
  output R6,
  output R5,
  output R4,
  output R3,
  output R2,
  output R1,
  output C0,
  output Cout,
  output C7
);

  wire somabits_3_cout, somabits_4_cout, somabits_5_cout, somabits_6_cout, somabits_7_cout, somabits_8_cout;

  Somabits somabits_1 (.a0(a7), .a1(b7), .Cin(C7), .S(R7), .Cout(Cout));
  Somabits somabits_2 (.a0(a6), .a1(b6), .Cin(somabits_3_cout), .S(R6), .Cout(C7));
  Somabits somabits_3 (.a0(a5), .a1(b5), .Cin(somabits_4_cout), .S(R5), .Cout(somabits_3_cout));
  Somabits somabits_4 (.a0(a4), .a1(b4), .Cin(somabits_5_cout), .S(R4), .Cout(somabits_4_cout));
  Somabits somabits_5 (.a0(a3), .a1(b3), .Cin(somabits_6_cout), .S(R3), .Cout(somabits_5_cout));
  Somabits somabits_6 (.a0(a2), .a1(b2), .Cin(somabits_7_cout), .S(R2), .Cout(somabits_6_cout));
  Somabits somabits_7 (.a0(a1), .a1(b1), .Cin(somabits_8_cout), .S(R1), .Cout(somabits_7_cout));
  Somabits somabits_8 (.a0(a0), .a1(b0), .Cin(Cin), .S(C0), .Cout(somabits_8_cout));
endmodule

module Somabits (
  input  a0,
  input  a1,
  input  Cin,
  output S,
  output Cout
);

  wire and_1_out, and_2_out, and_3_out, xor_1_out;

  xor xor_1 (xor_1_out, a0, a1);
  and and_1 (and_1_out, a0, a1);
  and and_2 (and_2_out, a0, Cin);
  and and_3 (and_3_out, a1, Cin);
  xor xor_2 (S, xor_1_out, Cin);
  or or_1 (Cout, and_1_out, and_2_out, and_3_out);
endmodule

module Selector1bit (
  input  S,
  input  a0,
  input  a1,
  output o
);

  wire and_1_out, and_2_out, not_1_out;

  not not_1 (not_1_out, S);
  and and_1 (and_1_out, S, a1);
  and and_2 (and_2_out, not_1_out, a0);
  or or_1 (o, and_2_out, and_1_out);
endmodule
