// Logisim project ep2.circ as structural Verilog: 8 circuits, main circuit CPU
module CPU (
  input  R,
  input  [7:0] entrada
);

  wire AC_igual_0, AC_maior_0, AC_menor_0, clock1, clock2, desvio, entrada_usuario, escrita, habilita_AC,
       imprime, leitura, not_1_out, OP, or_2_out, R_t, reseta, vr_desvio, vr_operacao;
  wire [7:0] AC, AC_ULA, conteudo_AC, conteudo_EE, EE, endereco, entrada_t, instrucao, PC, resultado;
  wire [15:0] controlled_buffer_2_out, dados, demultiplexer_1_out0;
  wire [15:8] demultiplexer_1_out1, IR_q;

  Clock clock_1 (.out(clock1));
  T_Flip_Flop t_ff_1 (.T(clock1), .clk(clock1), .Qn(clock2), .reset(R_t));  // open: Q, preset
  Register u_AC (.D(AC), .en(habilita_AC), .clk(clock1), .Q(conteudo_AC), .clr(R_t));
  RAM #(.asyncread("true"), .dataWidth(16)) ram_1 (
    .addr(endereco), .we(escrita), .oe(leitura), .clk(clock1), .din({{8{1'b0}}, entrada_t}), .dout(dados));
  assign entrada_t = not_1_out ? conteudo_AC : 8'bz;  // Controlled_Buffer controlled_buffer_1
  not not_1 (not_1_out, entrada_usuario);
  Multiplexer #(.enable("false"), .width(8)) multiplexer_1 (
    .in0(AC_ULA), .in1(entrada), .out(entrada_t), .sel(entrada_usuario));
  or or_1 (R_t, reseta, R);
  Demultiplexer #(.enable("false"), .width(16)) demultiplexer_1 (
    .out0(demultiplexer_1_out0), .out1({demultiplexer_1_out1, conteudo_EE}), .in(dados), .sel(habilita_AC));
  assign controlled_buffer_2_out = imprime ? dados : 16'bz;  // Controlled_Buffer controlled_buffer_2
  Register #(.width(16)) IR (.D(demultiplexer_1_out0), .clk(clock1), .Q({IR_q, EE}), .clr(R_t));  // open: en
  Hex_Digit_Display hex_digit_display_1 (.value(controlled_buffer_2_out[15:12]));  // open: dp
  Hex_Digit_Display hex_digit_display_2 (.value(controlled_buffer_2_out[11:8]));  // open: dp
  Hex_Digit_Display hex_digit_display_3 (.value(controlled_buffer_2_out[7:4]));  // open: dp
  Hex_Digit_Display hex_digit_display_4 (.value(controlled_buffer_2_out[3:0]));  // open: dp
  Multiplexer #(.enable("false"), .width(8)) multiplexer_2 (.in0(IR_q), .in1({8{1'b0}}), .out(instrucao), .sel(clock2));
  Multiplexer #(.enable("false"), .width(8)) multiplexer_3 (
    .in0(conteudo_EE), .in1(resultado), .out(AC), .sel(vr_operacao));
  Counter u_PC (.load(desvio), .D(EE), .Q(PC), .clk(clock2), .clr(R_t));  // open: count, carry, up
  Multiplexer #(.enable("false"), .width(8)) multiplexer_4 (.in0(EE), .in1(PC), .out(endereco), .sel(or_2_out));
  or or_2 (or_2_out, vr_desvio, clock2);
  UC uc_1 (
    .imprime(imprime), .reseta(reseta), .vr_desvio(vr_desvio), .leitura(leitura), .escrita(escrita),
    .vr_operacao(vr_operacao), .habilita_AC(habilita_AC), .desvio(desvio), .OP(OP),
    .entrada_usuario(entrada_usuario), .instrucao(instrucao), .AC_igual_0(AC_igual_0),
    .AC_menor_0(AC_menor_0), .AC_maior_0(AC_maior_0));
  ULA_main ula_main_1 (
    .A(conteudo_AC), .B(conteudo_EE), .OP(OP), .A_igual_B(AC_igual_0), .A_maior_B(AC_maior_0),
    .A_menor_B(AC_menor_0), .resultado(resultado));

  // Notes on the sheet:
  //   CONTROLE
  //   ACUMULADOR
  //   MEMÓRIA RAM & REGISTRADOR DE INSTRUÇÃO
  //   IMPRESSÃO
  //   ULA
  //   UC
  //   CONTADOR
endmodule

module UC (
  input  AC_maior_0,
  input  AC_igual_0,
  input  AC_menor_0,
  input  [7:0] instrucao,
  output leitura,
  output habilita_AC,
  output escrita,
  output vr_operacao,
  output OP,
  output imprime,
  output entrada_usuario,
  output reseta,
  output vr_desvio,
  output desvio
);

  wire and_1_out, and_2_out, and_3_out, i00, i0A, i0B, i0D, i0F, i01, i02, i03;

  nor nor_1 (leitura, i02, entrada_usuario);
  or or_1 (vr_desvio, i0A, i0B, i00, i0D, i0F);
  Decoder #(.enable("false"), .select(4)) decoder_1 (
    .out0(i00), .out1(i01), .out2(i02), .out3(i03), .out4(OP), .out7(entrada_usuario), .out8(imprime),
    .out9(reseta), .out10(i0A), .out11(i0B), .out13(i0D), .out15(i0F), .sel(instrucao[3:0]));  // open: out5, out6, out12, out14
  not not_1 (escrita, leitura);
  or or_2 (vr_operacao, i03, OP);
  or or_3 (habilita_AC, i01, vr_operacao);
  and and_1 (and_1_out, i0B, AC_maior_0);
  or or_4 (desvio, i0A, and_1_out, and_2_out, and_3_out);
  and and_2 (and_2_out, i0D, AC_igual_0);
  and and_3 (and_3_out, i0F, AC_menor_0);

  // Other names for the same wires on the sheet: i04 = OP; i07 = entrada_usuario; i08 = imprime; i09 = reseta

  // Notes on the sheet:
  //   LEITURA / ESCRITA
  //   DECODIFICADOR DE INSTRUÇÃO
  //   DESVIO
  //   SINAIS DE CONTROLE
  //   DESVIA PARA AC / INDICA OPERAÇÃO
  //   INSTRUÇÕES DIRETAS
endmodule

module somabits (
  input  a,
  input  b,
  input  cin,
  output s,
  output cout
);

  wire and_1_out, and_2_out, xor_1_out;

  xor xor_1 (xor_1_out, a, b);
  and and_1 (and_1_out, a, b);
  and and_2 (and_2_out, xor_1_out, cin);
  xor xor_2 (s, xor_1_out, cin);
  or or_1 (cout, and_1_out, and_2_out);
endmodule

module somador (
  input  [7:0] A,
  input  [7:0] B,
  input  OP,
  output [7:0] R,
  output c7,
  output c8
);

  wire somabits_1_cout, somabits_2_cout, somabits_3_cout, somabits_5_cout, somabits_6_cout, somabits_7_cout;

  somabits somabits_1 (.a(A[0]), .b(B[0]), .cin(OP), .s(R[0]), .cout(somabits_1_cout));
  somabits somabits_2 (.a(A[2]), .b(B[2]), .cin(somabits_5_cout), .s(R[2]), .cout(somabits_2_cout));
  somabits somabits_3 (.a(A[4]), .b(B[4]), .cin(somabits_6_cout), .s(R[4]), .cout(somabits_3_cout));
  somabits somabits_4 (.a(A[6]), .b(B[6]), .cin(somabits_7_cout), .s(R[6]), .cout(c7));
  somabits somabits_5 (.a(A[1]), .b(B[1]), .cin(somabits_1_cout), .s(R[1]), .cout(somabits_5_cout));
  somabits somabits_6 (.a(A[3]), .b(B[3]), .cin(somabits_2_cout), .s(R[3]), .cout(somabits_6_cout));
  somabits somabits_7 (.a(A[5]), .b(B[5]), .cin(somabits_3_cout), .s(R[5]), .cout(somabits_7_cout));
  somabits somabits_8 (.a(A[7]), .b(B[7]), .cin(c7), .s(R[7]), .cout(c8));

  // Other names for the same wires on the sheet: s0 = R[0]; s1 = R[1]; s2 = R[2]; s3 = R[3]; s4 = R[4]; s5 = R[5];
  //   s6 = R[6]; s7 = R[7]

  // Notes on the sheet:
  //   ENTRADA
  //   SAÍDA
  //   SOMA/SUBTRAÇÃO
endmodule

module comparabits (
  input  h,
  input  a,
  input  b,
  output a_igual_b,
  output a_maior_b,
  output b_maior_a
);

  wire not_1_out, not_2_out, not_3_out, xor_1_out;

  xor xor_1 (xor_1_out, a, b);
  and and_1 (a_maior_b, h, a, not_1_out);
  not not_1 (not_1_out, b);
  not not_2 (not_2_out, a);
  and and_2 (b_maior_a, h, not_2_out, b);
  not not_3 (not_3_out, xor_1_out);
  and and_3 (a_igual_b, not_3_out, h);
endmodule

module comparador (
  input  [7:0] A,
  input  [7:0] B,
  output c0,
  output c1,
  output c2,
  output c3,
  output c4,
  output c5
);

  wire a0_maior_b0, a1_maior_b1, a2_maior_b2, a3_maior_b3, a4_maior_b4, a5_maior_b5, a6_maior_b6,
       a7_maior_b7, and_1_out, and_2_out, b0_maior_a0, b1_maior_a1, b2_maior_a2, b3_maior_a3, b4_maior_a4,
       b5_maior_a5, b6_maior_a6, b7_maior_a7, comparabits_1_a_igual_b, comparabits_2_a_igual_b,
       comparabits_3_a_igual_b, comparabits_4_a_igual_b, comparabits_5_a_igual_b, comparabits_6_a_igual_b,
       comparabits_7_a_igual_b, not_1_out, not_2_out;

  nor nor_1 (c3, A[0], A[1], A[2], A[3], A[4], A[5], A[6], A[7]);
  comparabits comparabits_1 (
    .h(1'b1), .a(A[7]), .b(B[7]), .a_igual_b(comparabits_1_a_igual_b), .a_maior_b(a7_maior_b7),
    .b_maior_a(b7_maior_a7));
  comparabits comparabits_2 (
    .h(comparabits_5_a_igual_b), .a(A[5]), .b(B[5]), .a_igual_b(comparabits_2_a_igual_b),
    .a_maior_b(a5_maior_b5), .b_maior_a(b5_maior_a5));
  comparabits comparabits_3 (
    .h(comparabits_6_a_igual_b), .a(A[3]), .b(B[3]), .a_igual_b(comparabits_3_a_igual_b),
    .a_maior_b(a3_maior_b3), .b_maior_a(b3_maior_a3));
  comparabits comparabits_4 (
    .h(comparabits_7_a_igual_b), .a(A[1]), .b(B[1]), .a_igual_b(comparabits_4_a_igual_b),
    .a_maior_b(a1_maior_b1), .b_maior_a(b1_maior_a1));
  not not_1 (not_1_out, a7_maior_b7);
  not not_2 (not_2_out, b7_maior_a7);
  and and_1 (and_1_out, not_1_out, c0);
  and and_2 (and_2_out, not_2_out, c1);
  comparabits comparabits_5 (
    .h(comparabits_1_a_igual_b), .a(A[6]), .b(B[6]), .a_igual_b(comparabits_5_a_igual_b),
    .a_maior_b(a6_maior_b6), .b_maior_a(b6_maior_a6));
  comparabits comparabits_6 (
    .h(comparabits_2_a_igual_b), .a(A[4]), .b(B[4]), .a_igual_b(comparabits_6_a_igual_b),
    .a_maior_b(a4_maior_b4), .b_maior_a(b4_maior_a4));
  comparabits comparabits_7 (
    .h(comparabits_3_a_igual_b), .a(A[2]), .b(B[2]), .a_igual_b(comparabits_7_a_igual_b),
    .a_maior_b(a2_maior_b2), .b_maior_a(b2_maior_a2));
  comparabits comparabits_8 (
    .h(comparabits_4_a_igual_b), .a(A[0]), .b(B[0]), .a_igual_b(c2), .a_maior_b(a0_maior_b0),
    .b_maior_a(b0_maior_a0));
  or or_1 (c4, b7_maior_a7, and_1_out);
  or or_2 (c5, a7_maior_b7, and_2_out);
  or or_3 (c0, a7_maior_b7, a6_maior_b6, a5_maior_b5, a4_maior_b4, a3_maior_b3, a2_maior_b2, a1_maior_b1, a0_maior_b0);
  or or_4 (c1, b7_maior_a7, b6_maior_a6, b5_maior_a5, b4_maior_a4, b3_maior_a3, b2_maior_a2, b1_maior_a1, b0_maior_a0);

  // Other names for the same wires on the sheet: A_igual_B = c2; A_maior_B = c0; B_maior_A = c1

  // Notes on the sheet:
  //   ENTRADA
  //   SAÍDA
  //   COMPARAÇÃO
endmodule

module ULA (
  input  [7:0] A,
  input  [7:0] B,
  input  OP,
  output [7:0] R,
  output o1,
  output o2,
  output c0,
  output c1,
  output c2,
  output c3,
  output c4,
  output c5
);

  wire c7, c7_e_nc8_out, c8, c8_e_nc7_out, c8_e_nOP_out, not_2_out, not_3_out, not_4_out, not_5_out,
       OP_e_nc8_out;
  wire [7:0] multiplexer_1_out, not_1_out;

  Multiplexer #(.enable("false"), .width(8)) multiplexer_1 (
    .in0(B), .in1(not_1_out), .out(multiplexer_1_out), .sel(OP));
  assign not_1_out = ~B;  // NOT_Gate not_1, 8 bits wide
  and OP_e_nc8 (OP_e_nc8_out, OP, not_2_out);
  not not_2 (not_2_out, c8);
  and c8_e_nOP (c8_e_nOP_out, c8, not_3_out);
  not not_3 (not_3_out, OP);
  and c8_e_nc7 (c8_e_nc7_out, c8, not_4_out);
  not not_4 (not_4_out, c7);
  and c7_e_nc8 (c7_e_nc8_out, c7, not_5_out);
  not not_5 (not_5_out, c8);
  or or_1 (o1, OP_e_nc8_out, c8_e_nOP_out);
  or or_2 (o2, c8_e_nc7_out, c7_e_nc8_out);
  comparador comparador_1 (.A(A), .B(B), .c0(c0), .c1(c1), .c2(c2), .c3(c3), .c4(c4), .c5(c5));
  somador somador_1 (.A(A), .B(multiplexer_1_out), .OP(OP), .R(R), .c7(c7), .c8(c8));

  // Notes on the sheet:
  //   ENTRADA
  //   OVERFLOW
  //   COMPARAÇÃO
  //   ADIÇÃO/SUBTRAÇÃO
endmodule

module ULA_main (
  input  [7:0] A,
  input  [7:0] B,
  input  OP,
  output A_igual_B,
  output A_maior_B,
  output A_menor_B,
  output [7:0] resultado
);

  ULA ula_1 (.A(A), .c2(A_igual_B), .c4(A_maior_B), .c5(A_menor_B));  // open: B, OP, R, o1, o2, c0, c1, c3
  ULA ula_2 (.A(A), .B(B), .OP(OP), .R(resultado));  // open: o1, o2, c0, c1, c2, c3, c4, c5
endmodule
